# Fritzing sketch fritzing_diagram (saved by Fritzing 0.9.6b)
breadboards: 1

parts:
  U3 = ESP 32 DEVKIT DOIT
  R1 = Resistor [tolerance=±5% power=0.25 resistance=220 package=THT]
  S1 = Pushbutton [package="[THT]"]
  LED1 = LED - 5mm [color="Red (633nm)" current=0.030 package="5 mm [THT]"]

nets:
  N1: U3.D22, U3.D18, U3.D5, U3.D2, U3.D15, U3.GND, S1.Pin_1, S1.Pin_2, S1.Pin_3, S1.Pin_4, LED1.anode
  N2: R1.Pin_1, LED1.cathode
